// Logisim project dmux1-2.circ as structural Verilog: 1 circuit, main circuit main
module main (
  input  E0,
  input  C0,
  output S0,
  output S1
);

  wire not_1_out;

  not not_1 (not_1_out, C0);
  and and_1 (S0, not_1_out, E0);
  and and_2 (S1, C0, E0);
endmodule
