// Logisim project dmux1-4.circ as structural Verilog: 1 circuit, main circuit main
module main (
  input  E0,
  input  C0,
  input  C1,
  output S0,
  output S1,
  output S2,
  output S3
);

  wire not_1_out, not_2_out;

  not not_1 (not_1_out, C0);
  not not_2 (not_2_out, C1);
  and and_1 (S0, not_1_out, not_2_out, E0);
  and and_2 (S1, not_1_out, C1, E0);
  and and_3 (S2, C0, not_2_out, E0);
  and and_4 (S3, C0, C1, E0);
endmodule
