// Logisim project mux2-1.circ as structural Verilog: 1 circuit, main circuit main
module main (
  input  E0,
  input  E1,
  input  Control,
  output Saida
);

  wire and_1_out, and_2_out, not_1_out;

  not not_1 (not_1_out, Control);
  and and_1 (and_1_out, not_1_out, E0);
  and and_2 (and_2_out, Control, E1);
  or or_1 (Saida, and_1_out, and_2_out);
endmodule
