// Logisim project somador4bits.circ as structural Verilog: 1 circuit, main circuit main
module main (
  input  A3,
  input  A2,
  input  A1,
  input  A0,
  input  B3,
  input  B2,
  input  B1,
  input  B0
);

  wire decodificador_1_p5, decodificador_1_p6, decodificador_1_p7, decodificador_1_p8, decodificador_1_p9,
       decodificador_1_p10, decodificador_1_p11, main_1_s, main_2_cout, main_2_s, main_3_cout, main_3_s,
       main_4_cout, main_4_s;

  somadorCompleto_main main_1 (.A(A3), .B(B3), .Cin(main_2_cout), .S(main_1_s));  // open: Cout
  somadorCompleto_main main_2 (.A(A2), .B(B2), .Cin(main_3_cout), .S(main_2_s), .Cout(main_2_cout));
  somadorCompleto_main main_3 (.A(A1), .B(B1), .Cin(main_4_cout), .S(main_3_s), .Cout(main_3_cout));
  somadorCompleto_main main_4 (.A(A0), .B(B0), .Cin(1'b0), .S(main_4_s), .Cout(main_4_cout));
  // Decodificador decodificador_1: pin names not known; wires that end beside it: main_1_s, main_2_s, main_3_s, main_4_s, decodificador_1_p5, decodificador_1_p6, decodificador_1_p7, decodificador_1_p8, decodificador_1_p9, decodificador_1_p10, decodificador_1_p11
  _7_Segment_Display u_7_segment_display_1 (
    .g(decodificador_1_p11), .f(decodificador_1_p10), .a(decodificador_1_p5), .b(decodificador_1_p6),
    .e(decodificador_1_p9), .d(decodificador_1_p8), .c(decodificador_1_p7));  // open: dp
endmodule
