// Logisim project somadorSequencial.circ as structural Verilog: 1 circuit, main circuit main
module main (
  input  A3,
  input  A2,
  input  A1,
  input  A0,
  input  B3,
  input  B2,
  input  B1,
  input  B0,
  output S3,
  output S2,
  output S1,
  output S0
);

  wire main_2_cout, main_3_cout, main_4_cout;

  somadorCompleto_main main_1 (.A(A3), .B(B3), .Cin(main_2_cout), .S(S3));  // open: Cout
  somadorCompleto_main main_2 (.A(A2), .B(B2), .Cin(main_3_cout), .S(S2), .Cout(main_2_cout));
  somadorCompleto_main main_3 (.A(A1), .B(B1), .Cin(main_4_cout), .S(S1), .Cout(main_3_cout));
  somadorCompleto_main main_4 (.A(A0), .B(B0), .Cin(1'b0), .S(S0), .Cout(main_4_cout));
endmodule
