// Logisim project subtrator4bits.circ as structural Verilog: 1 circuit, main circuit main
module main (
  input  A3,
  input  A2,
  input  A1,
  input  A0,
  input  B3,
  input  B2,
  input  B1,
  input  B0
);

  wire decodificador_1_p5, decodificador_1_p6, decodificador_1_p7, decodificador_1_p8, decodificador_1_p9,
       decodificador_1_p10, decodificador_1_p11, subtratorcompleto_1_s, subtratorcompleto_2_cout,
       subtratorcompleto_2_s, subtratorcompleto_3_cout, subtratorcompleto_3_s, subtratorcompleto_4_cout,
       subtratorcompleto_4_s;

  subtratorCompleto subtratorcompleto_1 (
    .A(A3), .B(B3), .Cin(subtratorcompleto_2_cout), .S(subtratorcompleto_1_s));  // open: Cout
  subtratorCompleto subtratorcompleto_2 (
    .A(A2), .B(B2), .Cin(subtratorcompleto_3_cout), .S(subtratorcompleto_2_s), .Cout(subtratorcompleto_2_cout));
  subtratorCompleto subtratorcompleto_3 (
    .A(A1), .B(B1), .Cin(subtratorcompleto_4_cout), .S(subtratorcompleto_3_s), .Cout(subtratorcompleto_3_cout));
  subtratorCompleto subtratorcompleto_4 (
    .A(A0), .B(B0), .Cin(1'b0), .S(subtratorcompleto_4_s), .Cout(subtratorcompleto_4_cout));
  // Decodificador decodificador_1: pin names not known; wires that end beside it: subtratorcompleto_1_s, subtratorcompleto_2_s, subtratorcompleto_3_s, subtratorcompleto_4_s, decodificador_1_p5, decodificador_1_p6, decodificador_1_p7, decodificador_1_p8, decodificador_1_p9, decodificador_1_p10, decodificador_1_p11
  _7_Segment_Display u_7_segment_display_1 (
    .g(decodificador_1_p11), .f(decodificador_1_p10), .a(decodificador_1_p5), .b(decodificador_1_p6),
    .e(decodificador_1_p9), .d(decodificador_1_p8), .c(decodificador_1_p7));  // open: dp
endmodule
